// Logisim project cpu_logisim.circ as structural Verilog: 7 circuits, main circuit main
module main (
  input  in_1,
  output [31:0] out_2,
  output out_3,
  output [4:0] out_4,
  output [31:0] out_5,
  output out_6,
  output [4:0] out_7,
  output [31:0] out_8
);

  wire ALUBOp, BEQOp, clk, JALOp, JROp, RE, zero;
  wire [1:0] ALUOp, EXTOp, WAOp, WDOp;
  wire [31:0] ALUOut, EXT, JR, multiplexer_3_out, PC_4, RD;

  Clock clock_1 (.out(clk));
  IFU ifu_1 (
    .in_3(in_1), .out_10(out_2), .in_1(clk), .in_2(EXT), .beq(BEQOp), .zero(zero), .jal(JALOp), .out_9(PC_4),
    .in_8(JR), .jr(JROp));
  Control control_1 (
    .in_1(out_2[31:26]), .in_2(out_2[5:0]), .WDOp(WDOp), .BEQOp(BEQOp), .ALUBOp(ALUBOp), .EXTOp(EXTOp),
    .ALUOp(ALUOp), .DWE(out_6), .RE(RE), .RWE(out_3), .WAOp(WAOp), .JALOp(JALOp), .JROp(JROp));
  Multiplexer #(.select(2), .width(32), .enable("false")) multiplexer_1 (
    .in0({ALUOut[31:7], out_7, ALUOut[1:0]}), .in1(RD), .in2(PC_4), .out(out_5), .sel(WDOp));  // open: in3
  Multiplexer #(.select(2), .width(5), .enable("false")) multiplexer_2 (
    .in0(out_2[20:16]), .in1(out_2[15:11]), .in2({5{1'b1}}), .out(out_4), .sel(WAOp));  // open: in3
  GRF grf_1 (
    .in_2(out_2[25:21]), .in_3(out_2[20:16]), .in_4(out_4), .in_5(out_5), .in_6(in_1), .out_8(JR),
    .out_9(out_8), .in_1(out_3), .in_7(clk));
  EXT ext_1 (.in_1(out_2[15:0]), .out_3(EXT), .in_2(EXTOp));
  Multiplexer #(.width(32), .enable("false")) multiplexer_3 (
    .in0(EXT), .in1(out_8), .out(multiplexer_3_out), .sel(ALUBOp));
  ALU alu_1 (
    .in_2(JR), .in_3(multiplexer_3_out), .out_4({ALUOut[31:7], out_7, ALUOut[1:0]}), .out_5(zero),
    .in_1(ALUOp));
  DM dm_1 (.in_3(out_7), .in_5(out_8), .out_7(RD), .in_1(out_6), .in_2(RE), .in_4(in_1), .in_6(clk));

  // Other names for the same wires on the sheet: ALUOut[6:2] = out_7; MemAddr[4:0] = out_7; Func[5:0] = out_2[5:0];
  //   Instr[31:0] = out_2; MemData[31:0] = out_8; DWE = out_6; MemWrite = out_6; RegAddr[4:0] = out_4;
  //   RegData[31:0] = out_5; RegWrite = out_3; RWE = out_3; Reset = in_1
endmodule

module GRF (
  input  in_1,
  input  [4:0] in_2,
  input  [4:0] in_3,
  input  [4:0] in_4,
  input  [31:0] in_5,
  input  in_6,
  input  in_7,
  output [31:0] out_8,
  output [31:0] out_9
);

  wire W0, W1, W2, W3, W4, W5, W6, W7, W8, W9, W10, W11, W12, W13, W14, W15, W16, W17, W18, W19, W20, W21,
       W22, W23, W24, W25, W26, W27, W28, W29, W30, W31;
  wire [31:0] _0, _1, _2, _3, _4, _5, _6, _7, _8, _9, _10, _11, _12, _13, _14, _15, _16, _17, _18, _19, _20,
       _21, _22, _23, _24, _25, _26, _27, _28, _29, _30, _31, and_1_out;

  Multiplexer #(.select(5), .width(32)) multiplexer_1 (
    .in0(_0), .in1(_1), .in2(_2), .in3(_3), .in4(_4), .in5(_5), .in6(_6), .in7(_7), .in8(_8), .in9(_9),
    .in10(_10), .in11(_11), .in12(_12), .in13(_13), .in14(_14), .in15(_15), .in16(_16), .in17(_17),
    .in18(_18), .in19(_19), .in20(_20), .in21(_21), .in22(_22), .in23(_23), .in24(_24), .in25(_25),
    .in26(_26), .in27(_27), .in28(_28), .in29(_29), .in30(_30), .in31(_31), .out(out_8), .sel(in_2));  // open: en
  Multiplexer #(.select(5), .width(32)) multiplexer_2 (
    .in0(_0), .in1(_1), .in2(_2), .in3(_3), .in4(_4), .in5(_5), .in6(_6), .in7(_7), .in8(_8), .in9(_9),
    .in10(_10), .in11(_11), .in12(_12), .in13(_13), .in14(_14), .in15(_15), .in16(_16), .in17(_17),
    .in18(_18), .in19(_19), .in20(_20), .in21(_21), .in22(_22), .in23(_23), .in24(_24), .in25(_25),
    .in26(_26), .in27(_27), .in28(_28), .in29(_29), .in30(_30), .in31(_31), .out(out_9), .sel(in_3));  // open: en
  Demultiplexer #(.select(5), .disabled(0)) demultiplexer_1 (
    .out0(W0), .out1(W1), .out2(W2), .out3(W3), .out4(W4), .out5(W5), .out6(W6), .out7(W7), .out8(W8),
    .out9(W9), .out10(W10), .out11(W11), .out12(W12), .out13(W13), .out14(W14), .out15(W15), .out16(W16),
    .out17(W17), .out18(W18), .out19(W19), .out20(W20), .out21(W21), .out22(W22), .out23(W23), .out24(W24),
    .out25(W25), .out26(W26), .out27(W27), .out28(W28), .out29(W29), .out30(W30), .out31(W31), .in(in_1),
    .sel(in_4), .en(in_1));
  assign and_1_out = in_5 & {32{1'b0}};  // AND_Gate and_1, 32 bits wide
  Register #(.width(32)) register_1 (.D(and_1_out), .en(W0), .Q(_0), .clk(in_7), .clr(in_6));
  Register #(.width(32)) register_2 (.D(in_5), .en(W8), .Q(_8), .clk(in_7), .clr(in_6));
  Register #(.width(32)) register_3 (.D(in_5), .en(W16), .Q(_16), .clk(in_7), .clr(in_6));
  Register #(.width(32)) register_4 (.D(in_5), .en(W24), .Q(_24), .clk(in_7), .clr(in_6));
  Register #(.width(32)) register_5 (.D(in_5), .en(W1), .Q(_1), .clk(in_7), .clr(in_6));
  Register #(.width(32)) register_6 (.D(in_5), .en(W9), .Q(_9), .clk(in_7), .clr(in_6));
  Register #(.width(32)) register_7 (.D(in_5), .en(W17), .Q(_17), .clk(in_7), .clr(in_6));
  Register #(.width(32)) register_8 (.D(in_5), .en(W25), .Q(_25), .clk(in_7), .clr(in_6));
  Register #(.width(32)) register_9 (.D(in_5), .en(W2), .Q(_2), .clk(in_7), .clr(in_6));
  Register #(.width(32)) register_10 (.D(in_5), .en(W10), .Q(_10), .clk(in_7), .clr(in_6));
  Register #(.width(32)) register_11 (.D(in_5), .en(W18), .Q(_18), .clk(in_7), .clr(in_6));
  Register #(.width(32)) register_12 (.D(in_5), .en(W26), .Q(_26), .clk(in_7), .clr(in_6));
  Register #(.width(32)) register_13 (.D(in_5), .en(W3), .Q(_3), .clk(in_7), .clr(in_6));
  Register #(.width(32)) register_14 (.D(in_5), .en(W11), .Q(_11), .clk(in_7), .clr(in_6));
  Register #(.width(32)) register_15 (.D(in_5), .en(W19), .Q(_19), .clk(in_7), .clr(in_6));
  Register #(.width(32)) register_16 (.D(in_5), .en(W27), .Q(_27), .clk(in_7), .clr(in_6));
  Register #(.width(32)) register_17 (.D(in_5), .en(W4), .Q(_4), .clk(in_7), .clr(in_6));
  Register #(.width(32)) register_18 (.D(in_5), .en(W12), .Q(_12), .clk(in_7), .clr(in_6));
  Register #(.width(32)) register_19 (.D(in_5), .en(W20), .Q(_20), .clk(in_7), .clr(in_6));
  Register #(.width(32)) register_20 (.D(in_5), .en(W28), .Q(_28), .clk(in_7), .clr(in_6));
  Register #(.width(32)) register_21 (.D(in_5), .en(W5), .Q(_5), .clk(in_7), .clr(in_6));
  Register #(.width(32)) register_22 (.D(in_5), .en(W13), .Q(_13), .clk(in_7), .clr(in_6));
  Register #(.width(32)) register_23 (.D(in_5), .en(W21), .Q(_21), .clk(in_7), .clr(in_6));
  Register #(.width(32)) register_24 (.D(in_5), .en(W29), .Q(_29), .clk(in_7), .clr(in_6));
  Register #(.width(32)) register_25 (.D(in_5), .en(W6), .Q(_6), .clk(in_7), .clr(in_6));
  Register #(.width(32)) register_26 (.D(in_5), .en(W14), .Q(_14), .clk(in_7), .clr(in_6));
  Register #(.width(32)) register_27 (.D(in_5), .en(W22), .Q(_22), .clk(in_7), .clr(in_6));
  Register #(.width(32)) register_28 (.D(in_5), .en(W30), .Q(_30), .clk(in_7), .clr(in_6));
  Register #(.width(32)) register_29 (.D(in_5), .en(W7), .Q(_7), .clk(in_7), .clr(in_6));
  Register #(.width(32)) register_30 (.D(in_5), .en(W15), .Q(_15), .clk(in_7), .clr(in_6));
  Register #(.width(32)) register_31 (.D(in_5), .en(W23), .Q(_23), .clk(in_7), .clr(in_6));
  Register #(.width(32)) register_32 (.D(in_5), .en(W31), .Q(_31), .clk(in_7), .clr(in_6));

  // Other names for the same wires on the sheet: CLK = in_7; RA1[4:0] = in_2; RA2[4:0] = in_3; RD1[31:0] = out_8;
  //   RD2[31:0] = out_9; Reg_write = in_1; Reset = in_6; WA[4:0] = in_4; WD[31:0] = in_5
endmodule

module ALU (
  input  [1:0] in_1,
  input  [31:0] in_2,
  input  [31:0] in_3,
  output [31:0] out_4,
  output out_5
);

  wire [31:0] adder_1_out, or_1_out, subtractor_1_out;

  Adder #(.width(32)) adder_1 (.a(in_2), .b(in_3), .out(adder_1_out));  // open: cin, cout
  Subtractor #(.width(32)) subtractor_1 (.a(in_2), .b(in_3), .out(subtractor_1_out));  // open: bin, bout
  assign or_1_out = in_3 | in_2;  // OR_Gate or_1, 32 bits wide
  Comparator #(.width(32)) comparator_1 (.a(in_2), .b(in_3), .eq(out_5));  // open: gt, lt
  Multiplexer #(.select(2), .width(32)) multiplexer_1 (
    .in0(adder_1_out), .in1(subtractor_1_out), .in2(or_1_out), .in3(subtractor_1_out), .out(out_4), .sel(in_1));  // open: en

  // Other names for the same wires on the sheet: ALUOp[1:0] = in_1
endmodule

module EXT (
  input  [15:0] in_1,
  input  [1:0] in_2,
  output [31:0] out_3
);

  wire [31:0] bit_extender_1_out, bit_extender_2_out, bit_extender_3_out, bit_extender_4_out, shifter_1_out,
       shifter_2_out;

  assign bit_extender_1_out = {{16{in_1[15]}}, in_1};  // Bit_Extender bit_extender_1
  assign bit_extender_2_out = {{16{1'b0}}, in_1};  // Bit_Extender bit_extender_2
  assign bit_extender_3_out = {{16{in_1[15]}}, in_1};  // Bit_Extender bit_extender_3
  assign bit_extender_4_out = {{16{1'b0}}, in_1};  // Bit_Extender bit_extender_4
  Shifter #(.width(32)) shifter_1 (.in(bit_extender_1_out), .\dist (5'b00010), .out(shifter_1_out));
  Shifter #(.width(32)) shifter_2 (.in(bit_extender_4_out), .\dist (5'b10000), .out(shifter_2_out));
  Multiplexer #(.select(2), .width(32)) multiplexer_1 (
    .in0(bit_extender_2_out), .in1(bit_extender_3_out), .in2(shifter_1_out), .in3(shifter_2_out),
    .out(out_3), .sel(in_2));  // open: en
endmodule

module DM (
  input  in_1,
  input  in_2,
  input  [4:0] in_3,
  input  in_4,
  input  [31:0] in_5,
  input  in_6,
  output [31:0] out_7
);

  RAM #(.addrWidth(5), .dataWidth(32), .bus("separate")) ram_1 (
    .addr(in_3), .din(in_5), .data(out_7), .str(in_1), .clk(in_6), .ld(in_2), .clr(in_4));  // open: sel

  // Other names for the same wires on the sheet: clk = in_6; RE = in_2; Reset = in_4; WE = in_1
endmodule

module IFU (
  input  in_1,
  input  [31:0] in_2,
  input  in_3,
  input  beq,
  input  zero,
  input  jr,
  input  jal,
  input  [31:0] in_8,
  output [31:0] out_9,
  output [31:0] out_10
);

  wire and_1_out;
  wire [1:0] or_1_out;
  wire [31:0] adder_2_out, multiplexer_1_out, register_1_q;

  Register #(.width(32)) register_1 (.D(multiplexer_1_out), .Q(register_1_q), .clk(in_1), .clr(in_3));  // open: en
  Adder #(.width(32)) adder_1 (.a(32'h4), .b(register_1_q), .out(out_9));  // open: cin, cout
  Adder #(.width(32)) adder_2 (.a(out_9), .b(in_2), .out(adder_2_out));  // open: cin, cout
  and and_1 (and_1_out, beq, zero);
  ROM #(.addrWidth(5), .dataWidth(32)) rom_1 (.addr(register_1_q[6:2]), .data(out_10));  // open: sel
  or or_1 (or_1_out[0], and_1_out, jr);
  Multiplexer #(.select(2), .width(32), .enable("false")) multiplexer_1 (
    .in0(out_9), .in1(adder_2_out), .in2({register_1_q[31:28], out_10[25:0], 2'b00}), .in3(in_8),
    .out(multiplexer_1_out), .sel(or_1_out));
  or or_2 (or_1_out[1], jr, jal);

  // Other names for the same wires on the sheet: clk = in_1; jalext[25:0] = out_10[25:0]; Reset = in_3

  // Notes on the sheet:
  //   contents of rom_1 (hex, n*v repeats v):
  //   341c0000 341d0000 34013456 210821 3593769c 34dda539 3465c5dc 34be0ff1 3472af1d 35566602 35fe72a7
  //   3437ff23 37b9649e 3690bf9b 37fe4e0c 3711f49d 3c113bfe 3c057433 3c03c451 3c04c431 3c1c24d9 3c1bf0da
  //   3c0ccc68 3c0a118d 3c1021ea 3c0004d3 3c16115b 3c184f06 3c1215de 1000ffff
endmodule

module Control (
  input  [5:0] in_1,
  input  [5:0] in_2,
  output [1:0] WAOp,
  output [1:0] WDOp,
  output BEQOp,
  output ALUBOp,
  output [1:0] EXTOp,
  output [1:0] ALUOp,
  output DWE,
  output RE,
  output RWE,
  output JALOp,
  output JROp
);

  wire addu, and_10_out, lui, ori, subu;

  and and_1 (addu, in_2[0], ~in_2[1], ~in_2[2], ~in_2[3], ~in_2[4], in_2[5], ~in_1[0], ~in_1[1], ~in_1[2], ~in_1[3], ~in_1[4], ~in_1[5]);  // AND_Gate
  and and_2 (subu, in_2[0], in_2[1], ~in_2[2], ~in_2[3], ~in_2[4], in_2[5], ~in_1[0], ~in_1[1], ~in_1[2], ~in_1[3], ~in_1[4], ~in_1[5]);  // AND_Gate
  and and_3 (JROp, ~in_2[0], ~in_2[1], ~in_2[2], in_2[3], ~in_2[4], ~in_2[5], ~in_1[0], ~in_1[1], ~in_1[2], ~in_1[3], ~in_1[4], ~in_1[5]);  // AND_Gate
  and and_4 (ori, in_1[0], ~in_1[1], in_1[2], in_1[3], ~in_1[4], ~in_1[5]);  // AND_Gate
  and and_5 (RE, in_1[0], in_1[1], ~in_1[2], ~in_1[3], ~in_1[4], in_1[5]);  // AND_Gate
  and and_6 (DWE, in_1[0], in_1[1], ~in_1[2], in_1[3], ~in_1[4], in_1[5]);  // AND_Gate
  and and_7 (BEQOp, ~in_1[0], ~in_1[1], in_1[2], ~in_1[3], ~in_1[4], ~in_1[5]);  // AND_Gate
  and and_8 (lui, in_1[0], in_1[1], in_1[2], in_1[3], ~in_1[4], ~in_1[5]);  // AND_Gate
  and and_9 (JALOp, in_1[0], in_1[1], ~in_1[2], ~in_1[3], ~in_1[4], ~in_1[5]);  // AND_Gate
  and and_10 (and_10_out, ~in_1[0], ~in_1[1], ~in_1[2], ~in_1[3], ~in_1[4], ~in_1[5]);  // AND_Gate
  or or_1 (WAOp[0], addu, subu);
  or or_2 (ALUBOp, subu, addu, BEQOp);
  or or_3 (EXTOp[0], RE, DWE, lui);
  or or_4 (ALUOp[0], subu, BEQOp);
  or or_5 (EXTOp[1], BEQOp, lui);
  or or_6 (ALUOp[1], ori, BEQOp);
  or or_7 (RWE, ori, addu, subu, RE, lui, JALOp);

  assign WAOp[1] = JALOp;
  assign WDOp = {JALOp, RE};

  // Other names for the same wires on the sheet: beq = BEQOp; Func[5:0] = in_2; jr = JROp; OP[5:0] = in_1; sw = DWE;
  //   lw = RE; jal = JALOp
endmodule
