// Logisim project p03.circ as structural Verilog
module fsm (
  input  in_1,
  input  [1:0] in_2,
  output out_3
);

  wire and_1_out, and_2_out, and_3_out, and_4_out, and_5_out, clock_1_out, d_ff_1_q, d_ff_2_q, d_ff_3_q,
       or_1_out, or_2_out;

  and and_1 (and_1_out, in_2[0], ~in_2[1]);  // AND_Gate
  and and_2 (and_2_out, ~in_2[0], ~d_ff_2_q, d_ff_3_q);  // AND_Gate
  and and_3 (and_3_out, ~in_2[0], ~d_ff_2_q, d_ff_3_q);  // AND_Gate
  and and_4 (and_4_out, ~in_2[0], d_ff_2_q, ~d_ff_3_q);  // AND_Gate
  Clock clock_1 (.out(clock_1_out));
  or or_1 (or_1_out, and_1_out, and_2_out);
  or or_2 (or_2_out, and_3_out, and_4_out);
  D_Flip_Flop d_ff_1 (.clk(clock_1_out), .D(in_1), .Q(d_ff_1_q));  // open: Qn, preset, en, reset
  D_Flip_Flop d_ff_2 (.clk(clock_1_out), .D(or_1_out), .Q(d_ff_2_q), .reset(and_5_out));  // open: Qn, preset, en
  D_Flip_Flop d_ff_3 (.clk(clock_1_out), .D(or_2_out), .Q(d_ff_3_q), .reset(and_5_out));  // open: Qn, preset, en
  and and_5 (and_5_out, in_1, d_ff_1_q);
  and and_6 (out_3, or_1_out, or_2_out);
endmodule
