// Logisim project CPU.circ as structural Verilog: 8 circuits, main circuit main
module main (
  input  Reset,
  output [31:0] out_2,
  output out_3,
  output [4:0] out_4,
  output [31:0] out_5,
  output out_6,
  output [4:0] out_7,
  output [31:0] out_8
);

  wire ALUSrc, BEQ, Clk, MemRE, RegDst, StrReg, zero;
  wire [1:0] ALUOP, EXTOP;
  wire [31:0] alu_1_result, dm_1_rd, grf_1_rd1, multiplexer_2_out, offset, shifter_1_out;

  Clock u_Clk (.out(Clk));
  IFU ifu_1 (.Clk(Clk), .Reset(Reset), .Instr(out_2), .Offset(offset), .BEQ(BEQ), .zero(zero));
  // Probe on out_2[15:0]
  EXT ext_1 (.imm(out_2[15:0]), .Ext_imm(offset), .EXTOP(EXTOP));
  Controller controller_1 (
    .func(out_2[5:0]), .OP(out_2[31:26]), .BEQ(BEQ), .MemRE(MemRE), .StrReg(StrReg), .RegDst(RegDst),
    .MemWE(out_6), .RegWE(out_3), .ALUSrc(ALUSrc), .ALUOP(ALUOP), .EXTOP(EXTOP));
  Multiplexer #(.width(5), .disabled(0), .enable("false")) multiplexer_1 (
    .in0(out_2[20:16]), .in1(out_2[15:11]), .out(out_4), .sel(RegDst));
  GRF grf_1 (
    .Clk(Clk), .RA1(out_2[25:21]), .RA2(out_2[20:16]), .WA(out_4), .WD(out_5), .RD1(grf_1_rd1), .RD2(out_8),
    .WE(out_3), .Reset(Reset));
  Multiplexer #(.width(32), .enable("false")) multiplexer_2 (
    .in0(out_8), .in1(offset), .out(multiplexer_2_out), .sel(ALUSrc));
  ALU alu_1 (.A(grf_1_rd1), .B(multiplexer_2_out), .Zero(zero), .Result(alu_1_result), .ALUCtrl(ALUOP));
  Shifter #(.width(32), .shift("lr")) shifter_1 (.in(alu_1_result), .\dist (5'b00010), .out(shifter_1_out));
  Bit_Extender #(.in_width(32), .out_width(5)) bit_extender_1 (.in(shifter_1_out), .out(out_7));
  DM dm_1 (.Addr(out_7), .WD(out_8), .RD(dm_1_rd), .WE(out_6), .RE(MemRE), .Reset(Reset));
  Multiplexer #(.width(32), .enable("false")) multiplexer_3 (
    .in0(alu_1_result), .in1(dm_1_rd), .out(out_5), .sel(StrReg));

  // Other names for the same wires on the sheet: Instr[31:0] = out_2; func[5:0] = out_2[5:0]; MemAddr[4:0] = out_7;
  //   MemData[31:0] = out_8; MemWE = out_6; MemWrite = out_6; OP[5:0] = out_2[31:26]; RegAddr[4:0] = out_4;
  //   RegData[31:0] = out_5; RegWE = out_3; RegWrite = out_3
endmodule

module IFU (
  input  Clk,
  input  BEQ,
  input  zero,
  input  Reset,
  input  [31:0] Offset,
  output [31:0] Instr
);

  wire and_1_out;
  wire [4:0] bit_extender_1_out;
  wire [31:0] adder_1_out, adder_2_out, multiplexer_1_out, PC_q, shifter_1_out, shifter_2_out;

  Register #(.width(32)) PC (.D(multiplexer_1_out), .Q(PC_q), .clk(Clk), .clr(Reset));  // open: en
  Shifter #(.width(32), .shift("lr")) shifter_1 (.in(PC_q), .\dist (5'b00010), .out(shifter_1_out));
  Bit_Extender #(.in_width(32), .out_width(5)) bit_extender_1 (.in(shifter_1_out), .out(bit_extender_1_out));
  Adder #(.width(32)) adder_1 (.a(32'h4), .b(PC_q), .out(adder_1_out));  // open: cin, cout
  Shifter #(.width(32)) shifter_2 (.in(Offset), .\dist (5'b00010), .out(shifter_2_out));
  Adder #(.width(32)) adder_2 (.a(adder_1_out), .b(shifter_2_out), .out(adder_2_out));  // open: cin, cout
  ROM #(.addrWidth(5), .dataWidth(32)) rom_1 (.addr(bit_extender_1_out), .data(Instr));  // open: sel
  Multiplexer #(.width(32), .disabled(0), .enable("false")) multiplexer_1 (
    .in0(adder_1_out), .in1(adder_2_out), .out(multiplexer_1_out), .sel(and_1_out));
  and and_1 (and_1_out, BEQ, zero);

  // Notes on the sheet:
  //   contents of rom_1 (hex, n*v repeats v):
  //   341c0000 341d0000 340080f8 36ee0367 3593769c 34dda539 3465c5dc 34be0ff1 3472af1d 35566602 35fe72a7
  //   3437ff23 37b9649e 3690bf9b 37fe4e0c 3711f49d 3c113bfe 3c057433 3c03c451 3c04c431 3c1c24d9 3c1bf0da
  //   3c0ccc68 3c0a118d 3c1021ea 3c0004d3 3c16115b 3c184f06 3c1215de 1000ffff
endmodule

module GRF (
  input  Reset,
  input  WE,
  input  Clk,
  input  [4:0] RA1,
  input  [4:0] RA2,
  input  [4:0] WA,
  input  [31:0] WD,
  output [31:0] RD1,
  output [31:0] RD2
);

  wire W0, W1, W2, W3, W4, W5, W6, W7, W8, W9, W10, W11, W12, W13, W14, W15, W16, W17, W18, W19, W20, W21,
       W22, W23, W24, W25, W26, W27, W28, W29, W30, W31;
  wire [31:0] R0, R1, R2, R3, R4, R5, R6, R7, R8, R9, R10, R11, R12, R13, R14, R15, R16, R17, R18, R19, R20,
       R21, R22, R23, R24, R25, R26, R27, R28, R29, R30, R31;

  Register #(.width(32)) _0 (.D(WD), .en(W0), .Q(R0), .clk(Clk), .clr(1'b1));
  Register #(.width(32)) _8 (.D(WD), .en(W8), .Q(R8), .clk(Clk), .clr(Reset));
  Register #(.width(32)) _16 (.D(WD), .en(W16), .Q(R16), .clk(Clk), .clr(Reset));
  Register #(.width(32)) _24 (.D(WD), .en(W24), .Q(R24), .clk(Clk), .clr(Reset));
  Decoder #(.select(5), .disabled(0)) decoder_1 (
    .out0(W0), .out1(W1), .out2(W2), .out3(W3), .out4(W4), .out5(W5), .out6(W6), .out7(W7), .out8(W8),
    .out9(W9), .out10(W10), .out11(W11), .out12(W12), .out13(W13), .out14(W14), .out15(W15), .out16(W16),
    .out17(W17), .out18(W18), .out19(W19), .out20(W20), .out21(W21), .out22(W22), .out23(W23), .out24(W24),
    .out25(W25), .out26(W26), .out27(W27), .out28(W28), .out29(W29), .out30(W30), .out31(W31), .sel(WA),
    .en(WE));
  Register #(.width(32)) _1 (.D(WD), .en(W1), .Q(R1), .clk(Clk), .clr(Reset));
  Register #(.width(32)) _9 (.D(WD), .en(W9), .Q(R9), .clk(Clk), .clr(Reset));
  Register #(.width(32)) _17 (.D(WD), .en(W17), .Q(R17), .clk(Clk), .clr(Reset));
  Register #(.width(32)) _25 (.D(WD), .en(W25), .Q(R25), .clk(Clk), .clr(Reset));
  Register #(.width(32)) _2 (.D(WD), .en(W2), .Q(R2), .clk(Clk), .clr(Reset));
  Register #(.width(32)) _10 (.D(WD), .en(W10), .Q(R10), .clk(Clk), .clr(Reset));
  Register #(.width(32)) _18 (.D(WD), .en(W18), .Q(R18), .clk(Clk), .clr(Reset));
  Register #(.width(32)) _26 (.D(WD), .en(W26), .Q(R26), .clk(Clk), .clr(Reset));
  Register #(.width(32)) _3 (.D(WD), .en(W3), .Q(R3), .clk(Clk), .clr(Reset));
  Register #(.width(32)) _11 (.D(WD), .en(W11), .Q(R11), .clk(Clk), .clr(Reset));
  Register #(.width(32)) _19 (.D(WD), .en(W19), .Q(R19), .clk(Clk), .clr(Reset));
  Register #(.width(32)) _27 (.D(WD), .en(W27), .Q(R27), .clk(Clk), .clr(Reset));
  Register #(.width(32)) _4 (.D(WD), .en(W4), .Q(R4), .clk(Clk), .clr(Reset));
  Register #(.width(32)) _12 (.D(WD), .en(W12), .Q(R12), .clk(Clk), .clr(Reset));
  Register #(.width(32)) _20 (.D(WD), .en(W20), .Q(R20), .clk(Clk), .clr(Reset));
  Register #(.width(32)) _28 (.D(WD), .en(W28), .Q(R28), .clk(Clk), .clr(Reset));
  Register #(.width(32)) _5 (.D(WD), .en(W5), .Q(R5), .clk(Clk), .clr(Reset));
  Register #(.width(32)) _13 (.D(WD), .en(W13), .Q(R13), .clk(Clk), .clr(Reset));
  Register #(.width(32)) _21 (.D(WD), .en(W21), .Q(R21), .clk(Clk), .clr(Reset));
  Register #(.width(32)) _29 (.D(WD), .en(W29), .Q(R29), .clk(Clk), .clr(Reset));
  Multiplexer #(.select(5), .width(32), .enable("false")) multiplexer_1 (
    .in0(R0), .in1(R1), .in2(R2), .in3(R3), .in4(R4), .in5(R5), .in6(R6), .in7(R7), .in8(R8), .in9(R9),
    .in10(R10), .in11(R11), .in12(R12), .in13(R13), .in14(R14), .in15(R15), .in16(R16), .in17(R17),
    .in18(R18), .in19(R19), .in20(R20), .in21(R21), .in22(R22), .in23(R23), .in24(R24), .in25(R25),
    .in26(R26), .in27(R27), .in28(R28), .in29(R29), .in30(R30), .in31(R31), .out(RD1), .sel(RA1));
  Multiplexer #(.select(5), .width(32), .enable("false")) multiplexer_2 (
    .in0(R0), .in1(R1), .in2(R2), .in3(R3), .in4(R4), .in5(R5), .in6(R6), .in7(R7), .in8(R8), .in9(R9),
    .in10(R10), .in11(R11), .in12(R12), .in13(R13), .in14(R14), .in15(R15), .in16(R16), .in17(R17),
    .in18(R18), .in19(R19), .in20(R20), .in21(R21), .in22(R22), .in23(R23), .in24(R24), .in25(R25),
    .in26(R26), .in27(R27), .in28(R28), .in29(R29), .in30(R30), .in31(R31), .out(RD2), .sel(RA2));
  Register #(.width(32)) _6 (.D(WD), .en(W6), .Q(R6), .clk(Clk), .clr(Reset));
  Register #(.width(32)) _14 (.D(WD), .en(W14), .Q(R14), .clk(Clk), .clr(Reset));
  Register #(.width(32)) _22 (.D(WD), .en(W22), .Q(R22), .clk(Clk), .clr(Reset));
  Register #(.width(32)) _30 (.D(WD), .en(W30), .Q(R30), .clk(Clk), .clr(Reset));
  Register #(.width(32)) _7 (.D(WD), .en(W7), .Q(R7), .clk(Clk), .clr(Reset));
  Register #(.width(32)) _15 (.D(WD), .en(W15), .Q(R15), .clk(Clk), .clr(Reset));
  Register #(.width(32)) _23 (.D(WD), .en(W23), .Q(R23), .clk(Clk), .clr(Reset));
  Register #(.width(32)) _31 (.D(WD), .en(W31), .Q(R31), .clk(Clk), .clr(Reset));

  // Other names for the same wires on the sheet: WriteData[31:0] = WD
endmodule

module ALU (
  input  [1:0] ALUCtrl,
  input  [31:0] A,
  input  [31:0] B,
  output Zero,
  output [31:0] Result
);

  wire [31:0] adder_1_out, or_1_out, subtractor_1_out;

  Comparator #(.width(32)) comparator_1 (.a(A), .b(B), .eq(Zero));  // open: gt, lt
  assign or_1_out = A | B;  // OR_Gate or_1, 32 bits wide
  Adder #(.width(32)) adder_1 (.a(A), .b(B), .out(adder_1_out));  // open: cin, cout
  Subtractor #(.width(32)) subtractor_1 (.a(A), .b(B), .out(subtractor_1_out));  // open: bin, bout
  Multiplexer #(.select(2), .width(32), .enable("false")) multiplexer_1 (
    .in0(adder_1_out), .in1(subtractor_1_out), .in2(or_1_out), .out(Result), .sel(ALUCtrl));  // open: in3
endmodule

module DM (
  input  Reset,
  input  WE,
  input  RE,
  input  [4:0] Addr,
  input  [31:0] WD,
  output [31:0] RD
);

  RAM #(.addrWidth(5), .dataWidth(32), .bus("separate")) ram_1 (
    .addr(Addr), .din(WD), .data(RD), .str(WE), .clk(WE), .ld(RE), .clr(Reset));  // open: sel
endmodule

module EXT (
  input  [15:0] imm,
  input  [1:0] EXTOP,
  output [31:0] Ext_imm
);

  wire [31:0] bit_extender_1_out, shifter_1_out;

  assign bit_extender_1_out = {{16{1'b0}}, imm};  // Bit_Extender bit_extender_1
  Shifter #(.width(32)) shifter_1 (.in(bit_extender_1_out), .\dist (5'b10000), .out(shifter_1_out));
  Multiplexer #(.select(2), .width(32), .enable("false")) multiplexer_1 (
    .in0(bit_extender_1_out), .in1(shifter_1_out), .in2({{17{imm[15]}}, imm[14:0]}), .out(Ext_imm),
    .sel(EXTOP));  // open: in3
endmodule

module Controller (
  input  [5:0] func,
  input  [5:0] OP,
  output BEQ,
  output MemRE,
  output StrReg,
  output [1:0] EXTOP,
  output RegDst,
  output MemWE,
  output RegWE,
  output ALUSrc,
  output [1:0] ALUOP
);

  wire addu;

  and R_format (RegDst, ~OP[5], ~OP[4], ~OP[3], ~OP[2], ~OP[1], ~OP[0]);  // AND_Gate
  and ori (ALUOP[1], ~OP[5], ~OP[4], OP[3], OP[2], ~OP[1], OP[0]);  // AND_Gate
  and lw (MemRE, OP[5], ~OP[4], ~OP[3], ~OP[2], OP[1], OP[0]);  // AND_Gate
  and sw (MemWE, OP[5], ~OP[4], OP[3], ~OP[2], OP[1], OP[0]);  // AND_Gate
  and u_beq (BEQ, ~OP[5], ~OP[4], ~OP[3], OP[2], ~OP[1], ~OP[0]);  // AND_Gate
  and lui (EXTOP[0], ~OP[5], ~OP[4], OP[3], OP[2], OP[1], OP[0]);  // AND_Gate
  or u_RegWE (RegWE, ALUOP[1], RegDst, EXTOP[0], MemRE);
  or u_ALUSrc (ALUSrc, ALUOP[1], MemRE, EXTOP[0], MemWE);
  and u_addu (addu, func[5], ~func[4], ~func[3], ~func[2], ~func[1], func[0], RegDst);  // AND_Gate
  and subu (ALUOP[0], func[5], ~func[4], ~func[3], ~func[2], func[1], func[0], RegDst);  // AND_Gate

  assign EXTOP[1] = BEQ;
  assign StrReg = MemRE;

  // Other names for the same wires on the sheet: subu = ALUOP[0]; ori = ALUOP[1]; lui = EXTOP[0]; lw = MemRE;
  //   R_fomat = RegDst; sw = MemWE
endmodule

module testbench (
  output halt
);

  wire clk_out, comparator_1_gt, main_1_out_3, main_1_out_6;
  wire [3:0] counter_1_q;

  Clock clk (.out(clk_out));
  Counter #(.width(4), .max('hf)) counter_1 (
    .Q(counter_1_q), .carry(halt), .clk(clk_out));  // open: load, D, count, clr
  Comparator #(.width(4)) comparator_1 (.a(4'b0100), .b(counter_1_q), .gt(comparator_1_gt));  // open: eq, lt
  main main_1 (
    .Reset(comparator_1_gt), .out_3(main_1_out_3), .out_6(main_1_out_6));  // open: out_2, out_4, out_5, out_8, out_7
endmodule
