// Logisim project wfcpu.circ as structural Verilog: 7 circuits, main circuit main
module main (
  input  Reset,
  output [31:0] out_2,
  output out_3,
  output [4:0] out_4,
  output [31:0] out_5,
  output out_6,
  output [4:0] out_7,
  output [31:0] out_8
);

  wire ALUsrc, clk, MemRead, MemtoReg, nPC_sel, RegDst, zero;
  wire [1:0] ALUCon, EXTOp;
  wire [31:0] alu_1_out_4, dm_1_rd, grf_1_rd1, multiplexer_2_out, offset;

  // Probe on out_2
  Clock u_clk (.out(clk));
  IFU ifu_1 (.Reset(Reset), .offset(offset), .Branch(nPC_sel), .zero(zero), .out_6(out_2), .clk(clk));
  // Probe on out_2[31:26]
  Multiplexer #(.width(5)) multiplexer_1 (
    .in0(out_2[20:16]), .in1(out_2[15:11]), .out(out_4), .sel(RegDst));  // open: en
  EXT ext_1 (.in_1(out_2[15:0]), .EXTContor(EXTOp), .out_3(offset));
  Contorller contorller_1 (
    .func(out_2[5:0]), .ALUcontor(ALUCon), .RegDst(RegDst), .nPC_sel(nPC_sel), .EXTOp(EXTOp),
    .MemtoReg(MemtoReg), .MemWrite(out_6), .RegWrite(out_3), .ALUSrc(ALUsrc), .op(out_2[31:26]),
    .Memread(MemRead));
  GRF grf_1 (
    .RA1(out_2[25:21]), .RA2(out_2[20:16]), .WA(out_4), .WD(out_5), .RegWrite(out_3), .RD1(grf_1_rd1),
    .RD2(out_8), .Reseat(Reset), .clk(clk));
  Multiplexer #(.width(32)) multiplexer_2 (
    .in0(out_8), .in1(offset), .out(multiplexer_2_out), .sel(ALUsrc));  // open: en
  ALU alu_1 (.in_1(grf_1_rd1), .in_2(multiplexer_2_out), .ALUctro(ALUCon), .out_4(alu_1_out_4), .zero(zero));
  DM dm_1 (
    .A(alu_1_out_4), .WD(out_8), .WE(out_6), .RE(MemRead), .Reset(Reset), .RD(dm_1_rd), .out_7(out_7),
    .clk(clk));
  Multiplexer #(.width(32)) multiplexer_3 (.in0(alu_1_out_4), .in1(dm_1_rd), .out(out_5), .sel(MemtoReg));  // open: en

  // Other names for the same wires on the sheet: Instr[31:0] = out_2; func[5:0] = out_2[5:0]; MemAddr[4:0] = out_7;
  //   MemData[31:0] = out_8; MemWrite = out_6; RegAddr[4:0] = out_4; RegData[31:0] = out_5; RegWrite = out_3
endmodule

module IFU (
  input  clk,
  input  Reset,
  input  [31:0] offset,
  input  Branch,
  input  zero,
  output [31:0] out_6
);

  wire and_1_out;
  wire [31:0] adder_1_out, adder_2_out, multiplexer_1_out, register_1_q, shifter_1_out;

  Register #(.width(32)) register_1 (.D(multiplexer_1_out), .Q(register_1_q), .clk(clk), .clr(Reset));  // open: en
  ROM #(.addrWidth(5), .dataWidth(32)) rom_1 (.addr(register_1_q[6:2]), .data(out_6));  // open: sel
  Shifter #(.width(32)) shifter_1 (.in(offset), .\dist (5'b00010), .out(shifter_1_out));
  Adder #(.width(32)) adder_1 (.a(register_1_q), .b(32'h4), .out(adder_1_out));  // open: cin, cout
  Adder #(.width(32)) adder_2 (.a(adder_1_out), .b(shifter_1_out), .out(adder_2_out));  // open: cin, cout
  Multiplexer #(.width(32)) multiplexer_1 (
    .in0(adder_1_out), .in1(adder_2_out), .out(multiplexer_1_out), .sel(and_1_out));  // open: en
  and and_1 (and_1_out, Branch, zero);

  // Notes on the sheet:
  //   contents of rom_1 (hex, n*v repeats v):
  //   0 3c100020 3c110005 2119023 2519023 ac120000 8c120000 3c130003 2539023 2739821 ac130004 8c080004
  //   1084021 ac080004 8c100004 3c110001 1220fffe ac110008 2318823 8c090008 11290002 0 0 36100005 3411000c
  //   ae300000 0 8e240000 36310fff 1329021 0 1000ffff
endmodule

module GRF (
  input  [4:0] RA1,
  input  [4:0] RA2,
  input  RegWrite,
  input  [4:0] WA,
  input  [31:0] WD,
  input  Reseat,
  input  clk,
  output [31:0] RD1,
  output [31:0] RD2
);

  wire c0, c1, c2, c3, c4, c5, c6, c7, c8, c9, c10, c11, c12, c13, c14, c15, c16, c17, c18, c19, c20, c21,
       c22, c23, c24, c25, c26, c27, c28, c29, c30, c31;
  wire [31:0] _0, _1, _2, _3, _4, _5, _6, _7, _8, _9, _10, _11, _12, _13, _14, _15, _16, _17, _18, _19, _20,
       _21, _22, _23, _24, _25, _26, _27, _28, _29, _30, _31;

  Decoder #(.select(5), .disabled(0)) decoder_1 (
    .out0(c0), .out1(c1), .out2(c2), .out3(c3), .out4(c4), .out5(c5), .out6(c6), .out7(c7), .out8(c8),
    .out9(c9), .out10(c10), .out11(c11), .out12(c12), .out13(c13), .out14(c14), .out15(c15), .out16(c16),
    .out17(c17), .out18(c18), .out19(c19), .out20(c20), .out21(c21), .out22(c22), .out23(c23), .out24(c24),
    .out25(c25), .out26(c26), .out27(c27), .out28(c28), .out29(c29), .out30(c30), .out31(c31), .sel(WA),
    .en(RegWrite));
  Register #(.width(32)) register_1 (.D(WD), .en(c0), .Q(_0), .clk(clk), .clr(1'b1));
  Register #(.width(32)) register_2 (.D(WD), .en(c8), .Q(_8), .clk(clk), .clr(Reseat));
  Register #(.width(32)) register_3 (.D(WD), .en(c16), .Q(_16), .clk(clk), .clr(Reseat));
  Register #(.width(32)) register_4 (.D(WD), .en(c24), .Q(_24), .clk(clk), .clr(Reseat));
  Register #(.width(32)) register_5 (.D(WD), .en(c1), .Q(_1), .clk(clk), .clr(Reseat));
  Register #(.width(32)) register_6 (.D(WD), .en(c9), .Q(_9), .clk(clk), .clr(Reseat));
  Register #(.width(32)) register_7 (.D(WD), .en(c17), .Q(_17), .clk(clk), .clr(Reseat));
  Register #(.width(32)) register_8 (.D(WD), .en(c25), .Q(_25), .clk(clk), .clr(Reseat));
  Register #(.width(32)) register_9 (.D(WD), .en(c2), .Q(_2), .clk(clk), .clr(Reseat));
  Register #(.width(32)) register_10 (.D(WD), .en(c10), .Q(_10), .clk(clk), .clr(Reseat));
  Register #(.width(32)) register_11 (.D(WD), .en(c18), .Q(_18), .clk(clk), .clr(Reseat));
  Register #(.width(32)) register_12 (.D(WD), .en(c26), .Q(_26), .clk(clk), .clr(Reseat));
  Multiplexer #(.select(5), .width(32)) multiplexer_1 (
    .in0(_0), .in1(_1), .in2(_2), .in3(_3), .in4(_4), .in5(_5), .in6(_6), .in7(_7), .in8(_8), .in9(_9),
    .in10(_10), .in11(_11), .in12(_12), .in13(_13), .in14(_14), .in15(_15), .in16(_16), .in17(_17),
    .in18(_18), .in19(_19), .in20(_20), .in21(_21), .in22(_22), .in23(_23), .in24(_24), .in25(_25),
    .in26(_26), .in27(_27), .in28(_28), .in29(_29), .in30(_30), .in31(_31), .out(RD1), .sel(RA1));  // open: en
  Multiplexer #(.select(5), .width(32)) multiplexer_2 (
    .in0(_0), .in1(_1), .in2(_2), .in3(_3), .in4(_4), .in5(_5), .in6(_6), .in7(_7), .in8(_8), .in9(_9),
    .in10(_10), .in11(_11), .in12(_12), .in13(_13), .in14(_14), .in15(_15), .in16(_16), .in17(_17),
    .in18(_18), .in19(_19), .in20(_20), .in21(_21), .in22(_22), .in23(_23), .in24(_24), .in25(_25),
    .in26(_26), .in27(_27), .in28(_28), .in29(_29), .in30(_30), .in31(_31), .out(RD2), .sel(RA2));  // open: en
  Register #(.width(32)) register_13 (.D(WD), .en(c3), .Q(_3), .clk(clk), .clr(Reseat));
  Register #(.width(32)) register_14 (.D(WD), .en(c11), .Q(_11), .clk(clk), .clr(Reseat));
  Register #(.width(32)) register_15 (.D(WD), .en(c19), .Q(_19), .clk(clk), .clr(Reseat));
  Register #(.width(32)) register_16 (.D(WD), .en(c27), .Q(_27), .clk(clk), .clr(Reseat));
  Register #(.width(32)) register_17 (.D(WD), .en(c4), .Q(_4), .clk(clk), .clr(Reseat));
  Register #(.width(32)) register_18 (.D(WD), .en(c12), .Q(_12), .clk(clk), .clr(Reseat));
  Register #(.width(32)) register_19 (.D(WD), .en(c20), .Q(_20), .clk(clk), .clr(Reseat));
  Register #(.width(32)) register_20 (.D(WD), .en(c28), .Q(_28), .clk(clk), .clr(Reseat));
  Register #(.width(32)) register_21 (.D(WD), .en(c5), .Q(_5), .clk(clk), .clr(Reseat));
  Register #(.width(32)) register_22 (.D(WD), .en(c13), .Q(_13), .clk(clk), .clr(Reseat));
  Register #(.width(32)) register_23 (.D(WD), .en(c21), .Q(_21), .clk(clk), .clr(Reseat));
  Register #(.width(32)) register_24 (.D(WD), .en(c29), .Q(_29), .clk(clk), .clr(Reseat));
  Register #(.width(32)) register_25 (.D(WD), .en(c6), .Q(_6), .clk(clk), .clr(Reseat));
  Register #(.width(32)) register_26 (.D(WD), .en(c14), .Q(_14), .clk(clk), .clr(Reseat));
  Register #(.width(32)) register_27 (.D(WD), .en(c22), .Q(_22), .clk(clk), .clr(Reseat));
  Register #(.width(32)) register_28 (.D(WD), .en(c30), .Q(_30), .clk(clk), .clr(Reseat));
  Register #(.width(32)) register_29 (.D(WD), .en(c7), .Q(_7), .clk(clk), .clr(Reseat));
  Register #(.width(32)) register_30 (.D(WD), .en(c15), .Q(_15), .clk(clk), .clr(Reseat));
  Register #(.width(32)) register_31 (.D(WD), .en(c23), .Q(_23), .clk(clk), .clr(Reseat));
  Register #(.width(32)) register_32 (.D(WD), .en(c31), .Q(_31), .clk(clk), .clr(Reseat));
endmodule

module ALU (
  input  [31:0] in_1,
  input  [31:0] in_2,
  input  [1:0] ALUctro,
  output [31:0] out_4,
  output zero
);

  wire [31:0] adder_1_out, or_1_out, subtractor_1_out;

  Adder #(.width(32)) adder_1 (.a(in_1), .b(in_2), .out(adder_1_out));  // open: cin, cout
  Subtractor #(.width(32)) subtractor_1 (.a(in_1), .b(in_2), .out(subtractor_1_out));  // open: bin, bout
  assign or_1_out = in_2 | in_1;  // OR_Gate or_1, 32 bits wide
  Comparator #(.width(32)) comparator_1 (.a(in_1), .b(in_2), .eq(zero));  // open: gt, lt
  Multiplexer #(.select(2), .width(32)) multiplexer_1 (
    .in0(adder_1_out), .in1(subtractor_1_out), .in2(or_1_out), .out(out_4), .sel(ALUctro));  // open: in3, en
endmodule

module DM (
  input  [31:0] A,
  input  [31:0] WD,
  input  WE,
  input  clk,
  input  RE,
  input  Reset,
  output [4:0] out_7,
  output [31:0] RD
);

  RAM #(.addrWidth(5), .dataWidth(32), .bus("separate")) ram_1 (
    .addr(A[6:2]), .din(WD), .data(RD), .str(WE), .clk(clk), .ld(RE), .clr(Reset));  // open: sel

  assign out_7 = A[6:2];
endmodule

module EXT (
  input  [15:0] in_1,
  input  [1:0] EXTContor,
  output [31:0] out_3
);

  wire [31:0] bit_extender_1_out, bit_extender_2_out, shifter_1_out;

  assign bit_extender_1_out = {{16{in_1[15]}}, in_1};  // Bit_Extender bit_extender_1
  assign bit_extender_2_out = {{16{1'b0}}, in_1};  // Bit_Extender bit_extender_2
  Shifter #(.width(32)) shifter_1 (.in(bit_extender_2_out), .\dist (5'b10000), .out(shifter_1_out));
  Multiplexer #(.select(2), .width(32)) multiplexer_1 (
    .in0(bit_extender_2_out), .in1(shifter_1_out), .in2(bit_extender_1_out), .out(out_3), .sel(EXTContor));  // open: in3, en
endmodule

module Contorller (
  input  [5:0] op,
  input  [5:0] func,
  output [1:0] ALUcontor,
  output RegDst,
  output nPC_sel,
  output [1:0] EXTOp,
  output MemtoReg,
  output Memread,
  output MemWrite,
  output RegWrite,
  output ALUSrc
);

  wire add, not_1_out, not_2_out, not_3_out, not_4_out, not_5_out, not_6_out, not_7_out, not_8_out,
       not_9_out, not_10_out, not_11_out, not_12_out, not_13_out;

  not not_1 (not_1_out, op[0]);
  not not_2 (not_2_out, op[1]);
  not not_3 (not_3_out, op[2]);
  not not_4 (not_4_out, func[1]);
  not not_5 (not_5_out, func[2]);
  not not_6 (not_6_out, op[4]);
  not not_7 (not_7_out, op[3]);
  not not_8 (not_8_out, func[3]);
  not not_9 (not_9_out, func[2]);
  not not_10 (not_10_out, func[4]);
  not not_11 (not_11_out, func[3]);
  not not_12 (not_12_out, op[5]);
  not not_13 (not_13_out, func[4]);
  and and_1 (add, func[5], not_13_out, not_8_out, not_9_out, not_4_out, func[0], RegDst);
  and and_2 (ALUcontor[0], RegDst, func[5], not_10_out, not_11_out, not_5_out, func[1], func[0]);
  and R (RegDst, not_12_out, not_6_out, not_7_out, not_3_out, not_2_out, not_1_out);
  and ori (ALUcontor[1], not_12_out, not_6_out, op[3], op[2], not_2_out, op[0]);
  and lw (Memread, op[5], not_6_out, not_7_out, not_3_out, op[1], op[0]);
  and sw (MemWrite, op[5], not_6_out, op[3], not_3_out, op[1], op[0]);
  and beq (EXTOp[1], not_12_out, not_6_out, not_7_out, op[2], not_2_out, not_1_out);
  and lui (EXTOp[0], not_12_out, not_6_out, op[3], op[2], op[1], op[0]);
  or or_1 (RegWrite, ALUcontor[1], ALUcontor[0], RegDst, EXTOp[0], Memread);
  or or_2 (ALUSrc, ALUcontor[1], EXTOp[0], Memread, MemWrite);

  assign MemtoReg = Memread;
  assign nPC_sel = EXTOp[1];

  // Other names for the same wires on the sheet: sub = ALUcontor[0]; ori = ALUcontor[1]; lui = EXTOp[0];
  //   beq = EXTOp[1]; lw = Memread; R = RegDst; sw = MemWrite
endmodule
