// Logisim project fbnq1.circ as structural Verilog: 1 circuit, main circuit main
module main (
  input  [2:0] in_1,
  output [3:0] out_2
);

  wire clock_1_out, comparator_1_eq, comparator_2_eq, controlled_buffer_1_out, controlled_buffer_2_out,
       not_1_out;
  wire [2:0] counter_1_q;
  wire [3:0] adder_1_out, register_1_q, register_2_q;

  assign controlled_buffer_1_out = comparator_1_eq ? 1'b1 : 1'bz;  // Controlled_Buffer controlled_buffer_1
  Adder #(.width(4)) adder_1 (
    .a(register_1_q), .b(register_2_q), .out(adder_1_out), .cin(controlled_buffer_1_out));  // open: cout
  Counter #(.width(3), .max('h7)) counter_1 (
    .Q(counter_1_q), .clk(controlled_buffer_2_out));  // open: load, D, count, carry, clr
  Comparator #(.width(3), .mode("unsigned")) comparator_1 (
    .a(counter_1_q), .b(3'b001), .eq(comparator_1_eq));  // open: gt, lt
  Clock clock_1 (.out(clock_1_out));
  assign controlled_buffer_2_out = not_1_out ? clock_1_out : 1'bz;  // Controlled_Buffer controlled_buffer_2
  Register #(.width(4)) register_1 (.D(adder_1_out), .Q(register_1_q), .clk(controlled_buffer_2_out));  // open: en, clr
  Register #(.width(4)) register_2 (
    .D(register_1_q), .Q(register_2_q), .clk(controlled_buffer_2_out));  // open: en, clr
  Comparator #(.width(3), .mode("unsigned")) comparator_2 (
    .a(in_1), .b(counter_1_q), .eq(comparator_2_eq));  // open: gt, lt
  not not_1 (not_1_out, comparator_2_eq);
  assign out_2 = comparator_2_eq ? adder_1_out : 4'bz;  // Controlled_Buffer controlled_buffer_3
endmodule
