// Logisim project mod5.circ as structural Verilog
module mod5 (
  input  in_1,
  output out_2,
  output out_3,
  output out_4,
  output out_5,
  output out_6
);

  wire and_1_out, and_2_out, and_3_out, and_4_out, and_5_out, and_6_out, and_7_out, and_8_out, and_9_out,
       and_10_out, clock_1_out, d_ff_1_q, d_ff_2_q, d_ff_3_q, d_ff_4_q;

  and and_1 (and_1_out, ~1'b0, ~d_ff_1_q, ~d_ff_2_q, ~d_ff_3_q, ~d_ff_4_q, ~in_1);  // AND_Gate
  and and_2 (and_2_out, ~1'b0, d_ff_1_q, ~d_ff_2_q, ~d_ff_3_q, ~d_ff_4_q, ~in_1);  // AND_Gate
  and and_3 (and_3_out, ~d_ff_1_q, ~d_ff_2_q, ~d_ff_3_q, d_ff_4_q, ~in_1);  // AND_Gate
  and and_4 (and_4_out, ~1'b0, ~d_ff_1_q, ~d_ff_2_q, ~d_ff_3_q, ~d_ff_4_q, in_1);  // AND_Gate
  and and_5 (and_5_out, ~1'b0, d_ff_1_q, ~d_ff_2_q, ~d_ff_3_q, ~d_ff_4_q, in_1);  // AND_Gate
  and and_6 (and_6_out, ~1'b0, ~d_ff_1_q, ~d_ff_2_q, ~d_ff_3_q, d_ff_4_q, in_1);  // AND_Gate
  and and_7 (and_7_out, ~1'b0, ~d_ff_1_q, d_ff_2_q, ~d_ff_3_q, ~d_ff_4_q, in_1);  // AND_Gate
  and and_8 (and_8_out, ~1'b0, ~d_ff_1_q, ~d_ff_2_q, d_ff_3_q, ~d_ff_4_q, in_1);  // AND_Gate
  and and_9 (and_9_out, ~1'b0, ~d_ff_1_q, d_ff_2_q, ~d_ff_3_q, ~d_ff_4_q, ~in_1);  // AND_Gate
  and and_10 (and_10_out, ~1'b0, ~d_ff_1_q, ~d_ff_2_q, d_ff_3_q, ~d_ff_4_q, ~in_1);  // AND_Gate
  or or_1 (out_3, and_1_out, and_2_out, and_3_out);
  or or_2 (out_4, and_4_out, and_5_out, and_6_out);
  or or_3 (out_5, and_7_out, and_8_out);
  or or_4 (out_6, and_9_out, and_10_out);
  Clock clock_1 (.out(clock_1_out));
  D_Flip_Flop d_ff_1 (.clk(clock_1_out), .D(out_3), .Q(d_ff_1_q));  // open: Qn, preset, en, reset
  D_Flip_Flop d_ff_2 (.clk(clock_1_out), .D(out_4), .Q(d_ff_2_q));  // open: Qn, preset, en, reset
  D_Flip_Flop d_ff_3 (.clk(clock_1_out), .D(out_5), .Q(d_ff_3_q));  // open: Qn, preset, en, reset
  D_Flip_Flop d_ff_4 (.clk(clock_1_out), .D(out_6), .Q(d_ff_4_q));  // open: Qn, preset, en, reset

  assign out_2 = 1'b0;
endmodule
