// Logisim project swap.circ as structural Verilog
module swap (
  input  in_1,
  input  in_2,
  input  in_3,
  output out_4,
  output out_5
);

  wire and_1_out, and_2_out, and_3_out, and_4_out, controlled_buffer_1_out, controlled_buffer_2_out,
       controlled_buffer_3_out, controlled_buffer_4_out, not_1_out, not_2_out, not_3_out, not_4_out;

  assign controlled_buffer_1_out = not_1_out ? in_1 : 1'bz;  // Controlled_Buffer controlled_buffer_1
  not not_1 (not_1_out, in_3);
  assign controlled_buffer_2_out = in_3 ? in_1 : 1'bz;  // Controlled_Buffer controlled_buffer_2
  not not_2 (not_2_out, in_3);
  and and_1 (and_1_out, not_2_out, controlled_buffer_1_out);
  assign controlled_buffer_3_out = not_3_out ? in_2 : 1'bz;  // Controlled_Buffer controlled_buffer_3
  not not_3 (not_3_out, in_3);
  and and_2 (and_2_out, controlled_buffer_2_out, in_3);
  assign controlled_buffer_4_out = in_3 ? in_2 : 1'bz;  // Controlled_Buffer controlled_buffer_4
  and and_3 (and_3_out, controlled_buffer_4_out, in_3);
  not not_4 (not_4_out, in_3);
  and and_4 (and_4_out, controlled_buffer_3_out, not_4_out);
  or or_1 (out_4, and_1_out, and_3_out);
  or or_2 (out_5, and_2_out, and_4_out);
endmodule
